# Fritzing sketch teensy-pi (saved by Fritzing 0.8.5b)

parts:
  Teensy1 = Teensy 3.0
  Raspberry_Pi_B_rev1 = Raspberry Pi B rev2

nets:
  GND: Teensy1.GND, Raspberry_Pi_B_rev1.GND
  N1: Teensy1.D0, Raspberry_Pi_B_rev1.GPIO_14
  N2: Teensy1.D1, Raspberry_Pi_B_rev1.GPIO_15

notes:
  Micro-USB Keyboard Port
  Serial UART control
